// Digital circuit ImmDecoderMux.dig as structural Verilog
module ImmDecoderMux (
  input  [31:0] iw,
  input  [2:0] immSel,
  output [63:0] imm
);

  wire [63:0] immB_out, immI_out, immJ_out, immS_out, immU_out;

  BitExtender #(.inputBits(12), .outputBits(64)) immI (.in(iw[31:20]), .out(immI_out));
  BitExtender #(.inputBits(12), .outputBits(64)) immS (.in({iw[31:25], iw[11:7]}), .out(immS_out));
  BitExtender #(.inputBits(13), .outputBits(64)) immB (.in({iw[31], iw[7], iw[30:25], iw[11:8], 1'b0}), .out(immB_out));
  BitExtender #(.inputBits(32), .outputBits(64)) immU (.in({iw[31:12], {12{1'b0}}}), .out(immU_out));
  BitExtender #(.inputBits(21), .outputBits(64)) immJ (
    .in({iw[31], iw[19:12], iw[20], iw[30:21], 1'b0}), .out(immJ_out));
  Multiplexer #(.Selector_Bits(3), .Bits(64)) multiplexer_1 (
    .sel(immSel), .in_0(immI_out), .in_1(immS_out), .in_2(immB_out), .in_3(immU_out), .in_4(immJ_out),
    .in_5({64{1'b0}}), .in_6({64{1'b0}}), .in_7({64{1'b0}}), .out(imm));
endmodule
