// Digital circuit InstDecoder1.dig as structural Verilog
module InstDecoder1 (
  input  [31:0] IW,
  output ALUSrcB,
  output [2:0] ALUOp,
  output RFW
);

  wire add_2_eq, add_eq, addi_eq, and_1_out, and_2_out, I_type_eq, INUM_num, r_type_eq;

  Comparator #(.Bits(7)) I_type (.a(IW[6:0]), .b(7'b0010011), .eq(I_type_eq));  // open: gt, lt
  Comparator #(.Bits(3)) addi (.a(IW[14:12]), .b(3'b000), .eq(addi_eq));  // open: gt, lt
  Comparator #(.Bits(7)) r_type (.a(IW[6:0]), .b(7'b0110011), .eq(r_type_eq));  // open: gt, lt
  Comparator #(.Bits(3)) add (.a(IW[14:12]), .b(3'b000), .eq(add_eq));  // open: gt, lt
  Comparator #(.Bits(7)) add_2 (.a(IW[31:25]), .b({7{1'b0}}), .eq(add_2_eq));  // open: gt, lt
  and and_1 (and_1_out, I_type_eq, addi_eq);
  and and_2 (and_2_out, r_type_eq, add_eq, add_2_eq);
  PriorityEncoder INUM (.in0(and_1_out), .in1(and_2_out), .num(INUM_num));  // open: any
  ROM #(.AddrBits(1), .Bits(5)) rom_1 (.A(INUM_num), .sel(1'b1), .D({RFW, ALUOp, ALUSrcB}));

  // Other names for the same wires on the sheet: opc[6:0] = IW[6:0]; f3[2:0] = IW[14:12]; f7[6:0] = IW[31:25]

  // Notes on the sheet:
  //   contents of rom_1 (hex, n*v repeats v):
  //   11,10
endmodule
