// Digital circuit InstDecoder2.dig as structural Verilog
module InstDecoder2 (
  input  [31:0] iw,
  output ALUsrcB,
  output [2:0] ALUop,
  output RFW,
  output [2:0] immSel,
  output ALUsrcA,
  output [1:0] PCSel,
  output [1:0] WDSel,
  output [1:0] BUOp,
  output [1:0] MSZ,
  output MST,
  output MLD
);

  wire btype_1_eq, btype_2_eq, btype_3_eq, btype_4_eq, itype_1_eq, itype_2_eq, itype_3_eq, itype_4_eq,
       itype_5_eq, itype_6_eq, itype_7_eq, jtype_1_eq, rtype_1_eq, rtype_2_eq, rtype_3_eq, rtype_4_eq,
       rtype_5_eq, rtype_6_eq, rtype_7_eq, rtype_8_eq, stype_1_eq, stype_2_eq, stype_3_eq;
  wire [4:0] INUM_num;

  Itype itype_1 (.iw_funct3(iw[14:12]), .funct3(3'b000), .iw_opcode(iw[6:0]), .opcode(7'b0010011), .eq(itype_1_eq));
  Rtype rtype_1 (
    .iw_funct3(iw[14:12]), .funct3(3'b000), .iw_opcode(iw[6:0]), .opcode(7'b0110011), .iw_funct7(iw[31:25]),
    .funct7({7{1'b0}}), .eq(rtype_1_eq));
  Jtype jtype_1 (.iw_opcode(iw[6:0]), .opcode(7'b1101111), .eq(jtype_1_eq));
  Itype itype_2 (.iw_funct3(iw[14:12]), .funct3(3'b000), .iw_opcode(iw[6:0]), .opcode(7'b1100111), .eq(itype_2_eq));
  Rtype rtype_2 (
    .iw_funct3(iw[14:12]), .funct3(3'b000), .iw_opcode(iw[6:0]), .opcode(7'b0110011), .iw_funct7(iw[31:25]),
    .funct7(7'b0000001), .eq(rtype_2_eq));
  Rtype rtype_3 (
    .iw_funct3(iw[14:12]), .funct3(3'b100), .iw_opcode(iw[6:0]), .opcode(7'b0110011), .iw_funct7(iw[31:25]),
    .funct7(7'b0000001), .eq(rtype_3_eq));
  Rtype rtype_4 (
    .iw_funct3(iw[14:12]), .funct3(3'b101), .iw_opcode(iw[6:0]), .opcode(7'b0110011), .iw_funct7(iw[31:25]),
    .funct7({7{1'b0}}), .eq(rtype_4_eq));
  Rtype rtype_5 (
    .iw_funct3(iw[14:12]), .funct3(3'b001), .iw_opcode(iw[6:0]), .opcode(7'b0110011), .iw_funct7(iw[31:25]),
    .funct7({7{1'b0}}), .eq(rtype_5_eq));
  Itype itype_3 (.iw_funct3(iw[14:12]), .funct3(3'b101), .iw_opcode(iw[6:0]), .opcode(7'b0010011), .eq(itype_3_eq));
  Itype itype_4 (.iw_funct3(iw[14:12]), .funct3(3'b001), .iw_opcode(iw[6:0]), .opcode(7'b0010011), .eq(itype_4_eq));
  Btype btype_1 (.iw_funct3(iw[14:12]), .funct3(3'b000), .iw_opcode(iw[6:0]), .opcode(7'b1100011), .eq(btype_1_eq));
  Btype btype_2 (.iw_funct3(iw[14:12]), .funct3(3'b100), .iw_opcode(iw[6:0]), .opcode(7'b1100011), .eq(btype_2_eq));
  Btype btype_3 (.iw_funct3(iw[14:12]), .funct3(3'b101), .iw_opcode(iw[6:0]), .opcode(7'b1100011), .eq(btype_3_eq));
  Btype btype_4 (.iw_funct3(iw[14:12]), .funct3(3'b001), .iw_opcode(iw[6:0]), .opcode(7'b1100011), .eq(btype_4_eq));
  Rtype rtype_6 (
    .iw_funct3(iw[14:12]), .funct3(3'b111), .iw_opcode(iw[6:0]), .opcode(7'b0110011), .iw_funct7(iw[31:25]),
    .funct7({7{1'b0}}), .eq(rtype_6_eq));
  Rtype rtype_7 (
    .iw_funct3(iw[14:12]), .funct3(3'b110), .iw_opcode(iw[6:0]), .opcode(7'b0110011), .iw_funct7(iw[31:25]),
    .funct7({7{1'b0}}), .eq(rtype_7_eq));
  Rtype rtype_8 (
    .iw_funct3(iw[14:12]), .funct3(3'b000), .iw_opcode(iw[6:0]), .opcode(7'b0110011), .iw_funct7(iw[31:25]),
    .funct7(7'b0100000), .eq(rtype_8_eq));
  Itype itype_5 (.iw_funct3(iw[14:12]), .funct3(3'b000), .iw_opcode(iw[6:0]), .opcode(7'b0000011), .eq(itype_5_eq));
  Itype itype_6 (.iw_funct3(iw[14:12]), .funct3(3'b010), .iw_opcode(iw[6:0]), .opcode(7'b0000011), .eq(itype_6_eq));
  Itype itype_7 (.iw_funct3(iw[14:12]), .funct3(3'b011), .iw_opcode(iw[6:0]), .opcode(7'b0000011), .eq(itype_7_eq));
  Stype stype_1 (.iw_funct3(iw[14:12]), .funct3(3'b000), .iw_opcode(iw[6:0]), .opcode(7'b0100011), .eq(stype_1_eq));
  Stype stype_2 (.iw_funct3(iw[14:12]), .funct3(3'b010), .iw_opcode(iw[6:0]), .opcode(7'b0100011), .eq(stype_2_eq));
  Stype stype_3 (.iw_funct3(iw[14:12]), .funct3(3'b011), .iw_opcode(iw[6:0]), .opcode(7'b0100011), .eq(stype_3_eq));
  PriorityEncoder #(.Selector_Bits(5)) INUM (
    .in0(itype_1_eq), .in1(rtype_1_eq), .in2(jtype_1_eq), .in3(itype_2_eq), .in4(rtype_2_eq),
    .in5(rtype_3_eq), .in6(rtype_4_eq), .in7(rtype_5_eq), .in8(itype_3_eq), .in9(itype_4_eq),
    .in10(btype_1_eq), .in11(btype_2_eq), .in12(btype_3_eq), .in13(btype_4_eq), .in14(rtype_6_eq),
    .in15(rtype_7_eq), .in16(rtype_8_eq), .in17(itype_5_eq), .in18(itype_6_eq), .in19(itype_7_eq),
    .in20(stype_1_eq), .in21(stype_2_eq), .in22(stype_3_eq), .in23(1'b0), .in24(1'b0), .in25(1'b0),
    .in26(1'b0), .in27(1'b0), .in28(1'b0), .in29(1'b0), .in30(1'b0), .in31(1'b0), .num(INUM_num));  // open: any
  inum__control inum__control_1 (
    .MSZ(MSZ), .MST(MST), .MLD(MLD), .BUOp(BUOp), .immSel(immSel), .WDSel(WDSel), .PCSel(PCSel),
    .ALUsrcB(ALUsrcB), .ALUsrcA(ALUsrcA), .ALUop(ALUop), .RFW(RFW), .inum(INUM_num));  // open: bits

  // Other names for the same wires on the sheet: op[6:0] = iw[6:0]; f3[2:0] = iw[14:12]; f7[6:0] = iw[31:25]
endmodule
