// Digital circuit Store-Component.dig as structural Verilog
module Store_Component (
  input  [63:0] ADDR,
  input  [63:0] D_Current,
  input  [63:0] D_Write,
  input  [1:0] MSZ,
  output [63:0] Dout
);

  wire [63:0] multiplexer_1_out, multiplexer_2_out;

  Multiplexer #(.Bits(64)) multiplexer_1 (
    .sel(ADDR[2]), .in_0({D_Current[63:32], D_Write[31:0]}), .in_1({D_Write[31:0], D_Current[31:0]}),
    .out(multiplexer_1_out));
  Multiplexer #(.Selector_Bits(3), .Bits(64)) multiplexer_2 (
    .sel(ADDR[2:0]), .in_0({D_Current[63:8], D_Write[7:0]}),
    .in_1({D_Current[63:16], D_Write[7:0], D_Current[7:0]}),
    .in_2({D_Current[63:24], D_Write[7:0], D_Current[15:0]}),
    .in_3({D_Current[63:32], D_Write[7:0], D_Current[23:0]}),
    .in_4({D_Current[63:40], D_Write[7:0], D_Current[31:0]}),
    .in_5({D_Current[63:48], D_Write[7:0], D_Current[39:0]}),
    .in_6({D_Current[63:56], D_Write[7:0], D_Current[47:0]}), .in_7({D_Write[7:0], D_Current[55:0]}),
    .out(multiplexer_2_out));
  Multiplexer #(.Selector_Bits(2), .Bits(64)) multiplexer_3 (
    .sel(MSZ), .in_0(multiplexer_2_out), .in_1({64{1'b0}}), .in_2(multiplexer_1_out), .in_3(D_Write),
    .out(Dout));

  // Other names for the same wires on the sheet: BSel[2:0] = ADDR[2:0]; WSel = ADDR[2]; b0[7:0] = D_Current[7:0];
  //   w0[31:0] = D_Current[31:0]; b1[7:0] = D_Current[15:8]; b2[7:0] = D_Current[23:16]; b3[7:0] = D_Current[31:24];
  //   b4[7:0] = D_Current[39:32]; w1[31:0] = D_Current[63:32]; b5[7:0] = D_Current[47:40]; b6[7:0] = D_Current[55:48];
  //   b7[7:0] = D_Current[63:56]; BNew[7:0] = D_Write[7:0]; WNew[31:0] = D_Write[31:0]
endmodule
