// Digital circuit inum->control.dig as structural Verilog
module inum__control (
  input  [4:0] inum,
  output [18:0] bits,
  output [2:0] immSel,
  output [1:0] WDSel,
  output [1:0] PCSel,
  output ALUsrcB,
  output ALUsrcA,
  output [2:0] ALUop,
  output RFW,
  output [1:0] BUOp,
  output [1:0] MSZ,
  output MST,
  output MLD
);

  ROM #(.AddrBits(5), .Bits(19)) inum_to_control (
    .A(inum), .sel(1'b1), .D({bits[18], ALUop, ALUsrcA, ALUsrcB, bits[12:0]}));

  assign bits[17:13] = {ALUop, ALUsrcA, ALUsrcB};
  assign BUOp = bits[5:4];
  assign immSel = bits[8:6];
  assign MLD = bits[3];
  assign MST = bits[2];
  assign MSZ = bits[1:0];
  assign PCSel = bits[12:11];
  assign RFW = bits[18];
  assign WDSel = bits[10:9];

  // Notes on the sheet:
  //   contents of inum_to_control (hex, n*v repeats v):
  //   42000,40000,46b00,42a00,50000,68000,60000,58000,62000,5a000,7080
  //   ,7090,70a0,70b0,70000,78000,48000,42408,4240a,4240b,244c,244e,244f
endmodule
