// Digital circuit ALU.dig as structural Verilog
module ALU (
  input  [63:0] A,
  input  [63:0] B,
  input  [2:0] AluOp,
  output [63:0] R
);

  wire [63:0] add_1_s, and_1_out, div_1_q, mul_1_mul, or_1_out, sll_out, slr_out, sub_1_s;

  Add #(.Bits(64)) add_1 (.a(A), .b(B), .c_i(1'b0), .s(add_1_s));  // open: c_o
  Sub #(.Bits(64)) sub_1 (.a(A), .b(B), .c_i(1'b0), .s(sub_1_s));  // open: c_o
  Mul #(.Bits(32)) mul_1 (.a(A[31:0]), .b(B[31:0]), .mul(mul_1_mul));
  BarrelShifter #(.Bits(64)) sll (.in(A), .shift(B[6:0]), .out(sll_out));
  BarrelShifter #(.Bits(64), .direction("right")) slr (.in(A), .shift(B[6:0]), .out(slr_out));
  assign and_1_out = A & B;  // And and_1, 64 bits wide
  assign or_1_out = A | B;  // Or or_1, 64 bits wide
  Div #(.Bits(64)) div_1 (.a(A), .b(B), .q(div_1_q));  // open: r
  Multiplexer #(.Selector_Bits(3), .Bits(64)) multiplexer_1 (
    .sel(AluOp), .in_0(add_1_s), .in_1(sub_1_s), .in_2(mul_1_mul), .in_3(sll_out), .in_4(slr_out),
    .in_5(div_1_q), .in_6(and_1_out), .in_7(or_1_out), .out(R));
endmodule
