// Digital circuit Btype.dig as structural Verilog
module Btype (
  input  [2:0] iw_funct3,
  input  [2:0] funct3,
  input  [6:0] iw_opcode,
  input  [6:0] opcode,
  output eq
);

  wire comparator_1_eq, i_type_eq;

  Comparator #(.Bits(7)) i_type (.a(iw_opcode), .b(opcode), .eq(i_type_eq));  // open: gt, lt
  Comparator #(.Bits(3)) comparator_1 (.a(iw_funct3), .b(funct3), .eq(comparator_1_eq));  // open: gt, lt
  and and_1 (eq, i_type_eq, comparator_1_eq);
endmodule
