// Digital circuit InstructionWordDecoder.dig as structural Verilog
module InstructionWordDecoder (
  input  [31:0] IW,
  output [4:0] R1,
  output [4:0] R2,
  output [4:0] RD
);


  assign R1 = IW[19:15];
  assign R2 = IW[24:20];
  assign RD = IW[11:7];
endmodule
