// Digital circuit Jtype.dig as structural Verilog
module Jtype (
  input  [6:0] iw_opcode,
  input  [6:0] opcode,
  output eq
);

  Comparator #(.Bits(7)) j_type (.a(iw_opcode), .b(opcode), .eq(eq));  // open: gt, lt
endmodule
