// Digital circuit branch_unit.dig as structural Verilog
module branch_unit (
  input  [63:0] RD1,
  input  [63:0] RD2,
  input  [1:0] BUOp,
  output PCBr
);

  wire comparator_1_eq, comparator_1_lt, not_1_out, not_2_out;

  Comparator #(.Bits(64)) comparator_1 (.a(RD1), .b(RD2), .eq(comparator_1_eq), .lt(comparator_1_lt));  // open: gt
  not not_1 (not_1_out, comparator_1_lt);
  not not_2 (not_2_out, comparator_1_eq);
  Multiplexer #(.Selector_Bits(2)) multiplexer_1 (
    .sel(BUOp), .in_0(comparator_1_eq), .in_1(comparator_1_lt), .in_2(not_1_out), .in_3(not_2_out), .out(PCBr));
endmodule
