// Digital circuit lab06-part1.dig as structural Verilog
module lab06_part1 (
  input  CLK,
  input  EN,
  input  CLR,
  input  PROG,
  output [63:0] A0,
  output [63:0] A1,
  output [63:0] A2,
  output DONE
);

  wire ALUSrcB, and_2_out, CLK_t, RFW;
  wire [2:0] ALUOp;
  wire [4:0] rd, rs1, rs2;
  wire [31:0] IW;
  wire [63:0] add_1_s, alu_1_r, imm, multiplexer_1_out, PC, register_file_1_rd0, undriven, x0, x1, x2, x3,
       x4, x5, x6, x7, x8, x9, x13, x14, x15, x16, x17, x18, x19, x20, x21, x22, x23, x24, x25, x26, x27,
       x28, x29, x30, x31;

  // Probe on PC
  // Probe on IW
  // Probe on rs1
  // Probe on rs2
  // Probe on rd
  _64bitregister _64bitregister_1 (.D(add_1_s), .CLK(CLK_t), .EN(EN), .CLR(CLR), .Q(PC));
  Comparator #(.Bits(32)) End (.a(IW), .b(32'hc0001073), .eq(DONE));  // open: gt, lt
  and and_1 (CLK_t, CLK, ~DONE);  // And
  LED led_1 (.in(DONE));
  // Probe on x1
  // Probe on x2
  // Probe on x3
  // Probe on x4
  // Probe on x29
  InstMemory instmemory_1 (.PROG(PROG), .ADDR(PC[9:2]), .IW(IW));
  Add #(.Bits(64)) add_1 (.a(PC), .b(64'h4), .c_i(1'b0), .s(add_1_s));  // open: c_o
  // Probe on x5
  // Probe on x6
  // Probe on x7
  // Probe on x8
  // Probe on x30
  // Probe on x9
  // Probe on A1
  // Probe on A0
  // Probe on A2
  // Probe on x31
  // ImmDecoder immdecoder_1: pin names not known; wires that end beside it: IW, imm
  InstDecoder1 instdecoder1_1 (.IW(IW), .ALUSrcB(ALUSrcB), .ALUOp(ALUOp), .RFW(RFW));
  RegDecoder regdecoder_1 (.IW(IW), .RS1(rs1), .RS2(rs2), .RD(rd));
  // Probe on x13
  // Probe on x14
  // Probe on x15
  // Probe on x16
  // Probe on imm
  and and_2 (and_2_out, RFW, EN);
  // Probe on x17
  // Probe on x18
  // Probe on x19
  // Probe on x20
  register_file register_file_1 (
    .RR0(rs1), .RR1(rs2), .WR(rd), .WE(and_2_out), .CLR(CLR), .WD(alu_1_r), .CLK(CLK_t),
    .RD0(register_file_1_rd0), .x0(x0), .x1(x1), .x2(x2), .x3(x3), .x4(x4), .x5(x5), .x6(x6), .x7(x7),
    .x8(x8), .x9(x9), .x10(A0), .x11(A1), .x12(A2), .x13(x13), .x14(x14), .x15(x15), .x16(x16), .x17(x17),
    .x18(x18), .x19(x19), .x20(x20), .x21(x21), .x22(x22), .x23(x23), .x24(x24), .x25(x25), .x26(x26),
    .x27(x27), .x28(x28), .x29(x29), .x30(x30), .x31(x31));  // open: RD1
  // Probe on x21
  // Probe on x22
  // Probe on x23
  // Probe on x24
  // Probe on x25
  // Probe on x26
  // Probe on x27
  // Probe on x28
  Multiplexer #(.Bits(64)) multiplexer_1 (.sel(ALUSrcB), .in_0(undriven), .in_1(imm), .out(multiplexer_1_out));
  ALU alu_1 (.A(register_file_1_rd0), .B(multiplexer_1_out), .AluOp(ALUOp), .R(alu_1_r));

  // Other names for the same wires on the sheet: x10[63:0] = A0; x11[63:0] = A1; x12[63:0] = A2
endmodule

/* Test case part1:
CLK EN CLR PROG A0 A1 A2
0   0   1   0    x x x
1   0   1   0    x x x
0   1   0   0    x x x
while (!(DONE))
C   1  	0   0    x x x
end while
0   1   0   0    1 2 3
*/
