// Digital circuit project06.dig as structural Verilog
module project06 (
  input  [4:0] PROG,
  input  CLK,
  input  EN,
  input  CLR,
  output DONE,
  output [63:0] A0,
  output [63:0] A1,
  output [63:0] A2,
  output [63:0] A3
);

  wire ALUSrcA, ALUSrcB, and_2_out, CLK_t, MLD, MST, PCBr, RFW;
  wire [1:0] BUOp, MSZ, PCSel, WDSel;
  wire [2:0] ALUOp, IMMSel;
  wire [4:0] rd, rs1, rs2;
  wire [31:0] iw;
  wire [63:0] alu_1_r, imm, load_component_1_d, multiplexer_1_out, multiplexer_2_out, multiplexer_3_out,
       multiplexer_4_out, multiplexer_5_out, PC, PC_plus_4_s, ramdualport_1_d, register_file_1_rd0,
       register_file_1_rd1, store_component_1_dout, x0, x1, x2, x3, x4, x5, x6, x7, x8, x9, x14, x15, x16,
       x17, x18, x19, x20, x21, x22, x23, x24, x25, x26, x27, x28, x29, x30, x31;

  // Probe on PC
  // Probe on iw
  // Probe on rs1
  // Probe on rs2
  // Probe on rd
  // Probe on imm
  // Probe on x1
  // Probe on x2
  // Probe on x3
  // Probe on x4
  and and_1 (CLK_t, CLK, ~DONE);  // And
  Comparator #(.Bits(32)) comparator_1 (.a(iw), .b(32'hc0001073), .eq(DONE));  // open: gt, lt
  Multiplexer #(.Selector_Bits(2), .Bits(64)) multiplexer_1 (
    .sel(PCSel), .in_0(PC_plus_4_s), .in_1(alu_1_r), .in_2(multiplexer_2_out), .in_3({64{1'b0}}),
    .out(multiplexer_1_out));
  Multiplexer #(.Bits(64)) multiplexer_2 (.sel(PCBr), .in_0(PC_plus_4_s), .in_1(alu_1_r), .out(multiplexer_2_out));
  // Probe on x5
  // Probe on x6
  // Probe on x7
  // Probe on x8
  _64bitregister _64bitregister_1 (.D(multiplexer_1_out), .CLK(CLK_t), .EN(EN), .CLR(CLR), .Q(PC));
  // Probe on x9
  // Probe on A1
  // Probe on A0
  // Probe on A2
  Add #(.Bits(64)) PC_plus_4 (.a(PC), .b(64'h4), .c_i(1'b0), .s(PC_plus_4_s));  // open: c_o
  // Probe on A3
  // Probe on x14
  // Probe on x15
  // Probe on x16
  // inst_mem inst_mem_1: pin names not known; wires that end beside it: PROG, PC[10:2], iw
  // Probe on x17
  // Probe on x18
  // Probe on x19
  // Probe on x20
  // Probe on x21
  // Probe on x22
  // Probe on x23
  // Probe on x24
  InstDecoder2 instdecoder2_1 (
    .iw(iw), .ALUsrcB(ALUSrcB), .ALUop(ALUOp), .RFW(RFW), .immSel(IMMSel), .ALUsrcA(ALUSrcA), .PCSel(PCSel),
    .WDSel(WDSel), .BUOp(BUOp), .MSZ(MSZ), .MST(MST), .MLD(MLD));
  InstructionWordDecoder instructionworddecoder_1 (.IW(iw), .R1(rs1), .R2(rs2), .RD(rd));
  ImmDecoderMux immdecodermux_1 (.iw(iw), .immSel(IMMSel), .imm(imm));
  and and_2 (and_2_out, RFW, EN);
  // Probe on x25
  // Probe on x26
  // Probe on x27
  // Probe on x28
  Multiplexer #(.Selector_Bits(2), .Bits(64)) multiplexer_3 (
    .sel(WDSel), .in_0(alu_1_r), .in_1(PC_plus_4_s), .in_2(load_component_1_d), .in_3(load_component_1_d),
    .out(multiplexer_3_out));
  // Probe on x29
  // Probe on x30
  // Probe on x31
  register_file register_file_1 (
    .RR0(rs1), .RR1(rs2), .WR(rd), .WE(and_2_out), .CLR(CLR), .WD(multiplexer_3_out), .CLK(CLK_t),
    .RD0(register_file_1_rd0), .RD1(register_file_1_rd1), .x0(x0), .x1(x1), .x2(x2), .x3(x3), .x4(x4),
    .x5(x5), .x6(x6), .x7(x7), .x8(x8), .x9(x9), .x10(A0), .x11(A1), .x12(A2), .x13(A3), .x14(x14),
    .x15(x15), .x16(x16), .x17(x17), .x18(x18), .x19(x19), .x20(x20), .x21(x21), .x22(x22), .x23(x23),
    .x24(x24), .x25(x25), .x26(x26), .x27(x27), .x28(x28), .x29(x29), .x30(x30), .x31(x31));
  Multiplexer #(.Bits(64)) multiplexer_4 (
    .sel(ALUSrcA), .in_0(register_file_1_rd0), .in_1(PC), .out(multiplexer_4_out));
  Multiplexer #(.Bits(64)) multiplexer_5 (
    .sel(ALUSrcB), .in_0(register_file_1_rd1), .in_1(imm), .out(multiplexer_5_out));
  branch_unit branch_unit_1 (.RD1(register_file_1_rd0), .RD2(register_file_1_rd1), .BUOp(BUOp), .PCBr(PCBr));
  ALU alu_1 (.A(multiplexer_4_out), .B(multiplexer_5_out), .AluOp(ALUOp), .R(alu_1_r));
  Store_Component store_component_1 (
    .ADDR(alu_1_r), .D_Current(ramdualport_1_d), .D_Write(register_file_1_rd1), .MSZ(MSZ),
    .Dout(store_component_1_dout));
  RAMDualPort #(.AddrBits(7), .Bits(64)) ramdualport_1 (
    .A(alu_1_r[9:3]), .Din(store_component_1_dout), .str(MST), .C(CLK_t), .ld(MLD), .D(ramdualport_1_d));
  Load_Component load_component_1 (.ADDR(alu_1_r), .Din(ramdualport_1_d), .MSZ(MSZ), .D(load_component_1_d));

  // Other names for the same wires on the sheet: x10[63:0] = A0; x11[63:0] = A1; x12[63:0] = A2; x13[63:0] = A3
endmodule

/* Test case 00-unit-add-i:
CLR EN CLK PROG A0 A1 A2 A3
1   0   0   x    x    x    x    x
0   0   0   x    x    x    x    x
while (!(DONE))
0   1   C   0    x    x    x    x
end while
0   1   0   0 3  0  0  0
*/

/* Test case 11-unit-bge:
CLR EN CLK PROG A0 A1 A2 A3
1   0   0   x    x    x    x    x
0   0   0   x    x    x    x    x
while (!(DONE))
0   1   C   11    x    x    x    x
end while
0   1   0   11 2  1  0  0
*/

/* Test case 14-unit-sb-lb:
CLR EN CLK PROG A0 A1 A2 A3
1   0   0   x    x    x    x    x
0   0   0   x    x    x    x    x
while (!(DONE))
0   1   C   14    x    x    x    x
end while
0   1   0   14 99  0  0  0
*/

/* Test case 01-unit-add-r:
CLR EN CLK PROG A0 A1 A2 A3
1   0   0   x    x    x    x    x
0   0   0   x    x    x    x    x
while (!(DONE))
0   1   C   1    x    x    x    x
end while
0   1   0   1 9  6  0  0
*/

/* Test case 15-prog-quadratic:
CLR EN CLK PROG A0 A1 A2 A3
1   0   0   x    x    x    x    x
0   0   0   x    x    x    x    x
while (!(DONE))
0   1   C   15    x    x    x    x
end while
0   1   0   15 25  3  4  5
*/

/* Test case 13-unit-sw-lw:
CLR EN CLK PROG A0 A1 A2 A3
1   0   0   x    x    x    x    x
0   0   0   x    x    x    x    x
while (!(DONE))
0   1   C   13    x    x    x    x
end while
0   1   0   13 99  0  0  0
*/

/* Test case 02-unit-jal:
CLR EN CLK PROG A0 A1 A2 A3
1   0   0   x    x    x    x    x
0   0   0   x    x    x    x    x
while (!(DONE))
0   1   C   2    x    x    x    x
end while
0   1   0   2 3  2  0  0
*/

/* Test case 16-prog-get-bitseq:
CLR EN CLK PROG A0 A1 A2 A3
1   0   0   x    x    x    x    x
0   0   0   x    x    x    x    x
while (!(DONE))
0   1   C   16    x    x    x    x
end while
0   1   0   16 6  12  15  0
*/

/* Test case 12-unit-sd-ld:
CLR EN CLK PROG A0 A1 A2 A3
1   0   0   x    x    x    x    x
0   0   0   x    x    x    x    x
while (!(DONE))
0   1   C   12    x    x    x    x
end while
0   1   0   12 99  0  0  0
*/

/* Test case 03-unit-mul:
CLR EN CLK PROG A0 A1 A2 A3
1   0   0   x    x    x    x    x
0   0   0   x    x    x    x    x
while (!(DONE))
0   1   C   3    x    x    x    x
end while
0   1   0   3 21  7  0  0
*/

/* Test case 04-unit-sll-r:
CLR EN CLK PROG A0 A1 A2 A3
1   0   0   x    x    x    x    x
0   0   0   x    x    x    x    x
while (!(DONE))
0   1   C   4    x    x    x    x
end while
0   1   0   4 4  1  2  0
*/

/* Test case 19-prog-to-upper:
CLR EN CLK PROG A0 A1 A2 A3
1   0   0   x    x    x    x    x
0   0   0   x    x    x    x    x
while (!(DONE))
0   1   C   19    x    x    x    x
end while
0   1   0   19 5066355251797426176  1014  0  0
*/

/* Test case 05-unit-srl-r:
CLR EN CLK PROG A0 A1 A2 A3
1   0   0   x    x    x    x    x
0   0   0   x    x    x    x    x
while (!(DONE))
0   1   C   5    x    x    x    x
end while
0   1   0   5 4  8  1  0
*/

/* Test case 06-unit-slli:
CLR EN CLK PROG A0 A1 A2 A3
1   0   0   x    x    x    x    x
0   0   0   x    x    x    x    x
while (!(DONE))
0   1   C   6    x    x    x    x
end while
0   1   0   6 8  1  0  0
*/

/* Test case 07-unit-srli:
CLR EN CLK PROG A0 A1 A2 A3
1   0   0   x    x    x    x    x
0   0   0   x    x    x    x    x
while (!(DONE))
0   1   C   7    x    x    x    x
end while
0   1   0   7 8  32  0  0
*/

/* Test case 08-unit-j:
CLR EN CLK PROG A0 A1 A2 A3
1   0   0   x    x    x    x    x
0   0   0   x    x    x    x    x
while (!(DONE))
0   1   C   8    x    x    x    x
end while
0   1   0   8 1  0  0  0
*/

/* Test case 09-unit-beq:
CLR EN CLK PROG A0 A1 A2 A3
1   0   0   x    x    x    x    x
0   0   0   x    x    x    x    x
while (!(DONE))
0   1   C   9    x    x    x    x
end while
0   1   0   9 1  1  0  0
*/

/* Test case 10-unit-blt:
CLR EN CLK PROG A0 A1 A2 A3
1   0   0   x    x    x    x    x
0   0   0   x    x    x    x    x
while (!(DONE))
0   1   C   10    x    x    x    x
end while
0   1   0   10 1  2  0  0
*/
