// Digital circuit register-file.dig as structural Verilog
module register_file (
  input  [4:0] RR0,
  input  [4:0] RR1,
  input  [63:0] WD,
  input  WE,
  input  CLR,
  input  CLK,
  input  [4:0] WR,
  output [63:0] RD0,
  output [63:0] RD1,
  output [63:0] x1,
  output [63:0] x2,
  output [63:0] x3,
  output [63:0] x4,
  output [63:0] x5,
  output [63:0] x6,
  output [63:0] x7,
  output [63:0] x8,
  output [63:0] x9,
  output [63:0] x10,
  output [63:0] x11,
  output [63:0] x12,
  output [63:0] x13,
  output [63:0] x14,
  output [63:0] x15,
  output [63:0] x16,
  output [63:0] x17,
  output [63:0] x18,
  output [63:0] x19,
  output [63:0] x20,
  output [63:0] x21,
  output [63:0] x22,
  output [63:0] x23,
  output [63:0] x24,
  output [63:0] x25,
  output [63:0] x26,
  output [63:0] x27,
  output [63:0] x28,
  output [63:0] x29,
  output [63:0] x30,
  output [63:0] x31,
  output [63:0] x0
);

  wire EN0, EN1, EN2, EN3, EN4, EN5, EN6, EN7, EN8, EN9, EN10, EN11, EN12, EN13, EN14, EN15, EN16, EN17,
       EN18, EN19, EN20, EN21, EN22, EN23, EN24, EN25, EN26, EN27, EN28, EN29, EN30;
  wire [4:0] multiplexer_1_out;

  Multiplexer #(.Bits(5)) multiplexer_1 (.sel(WE), .in_0({5{1'b0}}), .in_1(WR), .out(multiplexer_1_out));
  Decoder #(.Selector_Bits(5)) decoder_1 (
    .sel(multiplexer_1_out), .out_1(EN0), .out_2(EN1), .out_3(EN2), .out_4(EN3), .out_5(EN4), .out_6(EN5),
    .out_7(EN6), .out_8(EN7), .out_9(EN8), .out_10(EN9), .out_11(EN10), .out_12(EN11), .out_13(EN12),
    .out_14(EN13), .out_15(EN14), .out_16(EN15), .out_17(EN16), .out_18(EN17), .out_19(EN18), .out_20(EN19),
    .out_21(EN20), .out_22(EN21), .out_23(EN22), .out_24(EN23), .out_25(EN24), .out_26(EN25), .out_27(EN26),
    .out_28(EN27), .out_29(EN28), .out_30(EN29), .out_31(EN30));  // open: out_0
  Multiplexer #(.Selector_Bits(5), .Bits(64)) multiplexer_2 (
    .sel(RR0), .in_0({64{1'b0}}), .in_1(x1), .in_2(x2), .in_3(x3), .in_4(x4), .in_5(x5), .in_6(x6),
    .in_7(x7), .in_8(x8), .in_9(x9), .in_10(x10), .in_11(x11), .in_12(x12), .in_13(x13), .in_14(x14),
    .in_15(x15), .in_16(x16), .in_17(x17), .in_18(x18), .in_19(x19), .in_20(x20), .in_21(x21), .in_22(x22),
    .in_23(x23), .in_24(x24), .in_25(x25), .in_26(x26), .in_27(x27), .in_28(x28), .in_29(x29), .in_30(x30),
    .in_31(x31), .out(RD0));
  Multiplexer #(.Selector_Bits(5), .Bits(64)) multiplexer_3 (
    .sel(RR1), .in_0({64{1'b0}}), .in_1(x1), .in_2(x2), .in_3(x3), .in_4(x4), .in_5(x5), .in_6(x6),
    .in_7(x7), .in_8(x8), .in_9(x9), .in_10(x10), .in_11(x11), .in_12(x12), .in_13(x13), .in_14(x14),
    .in_15(x15), .in_16(x16), .in_17(x17), .in_18(x18), .in_19(x19), .in_20(x20), .in_21(x21), .in_22(x22),
    .in_23(x23), .in_24(x24), .in_25(x25), .in_26(x26), .in_27(x27), .in_28(x28), .in_29(x29), .in_30(x30),
    .in_31(x31), .out(RD1));
  _64bitregister _64bitregister_1 (.D(WD), .CLK(CLK), .EN(EN0), .CLR(CLR), .Q(x1));
  _64bitregister _64bitregister_2 (.D(WD), .CLK(CLK), .EN(EN1), .CLR(CLR), .Q(x2));
  _64bitregister _64bitregister_3 (.D(WD), .CLK(CLK), .EN(EN2), .CLR(CLR), .Q(x3));
  _64bitregister _64bitregister_4 (.D(WD), .CLK(CLK), .EN(EN3), .CLR(CLR), .Q(x4));
  _64bitregister _64bitregister_5 (.D(WD), .CLK(CLK), .EN(EN4), .CLR(CLR), .Q(x5));
  _64bitregister _64bitregister_6 (.D(WD), .CLK(CLK), .EN(EN5), .CLR(CLR), .Q(x6));
  _64bitregister _64bitregister_7 (.D(WD), .CLK(CLK), .EN(EN6), .CLR(CLR), .Q(x7));
  _64bitregister _64bitregister_8 (.D(WD), .CLK(CLK), .EN(EN7), .CLR(CLR), .Q(x8));
  _64bitregister _64bitregister_9 (.D(WD), .CLK(CLK), .EN(EN8), .CLR(CLR), .Q(x9));
  _64bitregister _64bitregister_10 (.D(WD), .CLK(CLK), .EN(EN9), .CLR(CLR), .Q(x10));
  _64bitregister _64bitregister_11 (.D(WD), .CLK(CLK), .EN(EN10), .CLR(CLR), .Q(x11));
  _64bitregister _64bitregister_12 (.D(WD), .CLK(CLK), .EN(EN11), .CLR(CLR), .Q(x12));
  _64bitregister _64bitregister_13 (.D(WD), .CLK(CLK), .EN(EN12), .CLR(CLR), .Q(x13));
  _64bitregister _64bitregister_14 (.D(WD), .CLK(CLK), .EN(EN13), .CLR(CLR), .Q(x14));
  _64bitregister _64bitregister_15 (.D(WD), .CLK(CLK), .EN(EN14), .CLR(CLR), .Q(x15));
  _64bitregister _64bitregister_16 (.D(WD), .CLK(CLK), .EN(EN15), .CLR(CLR), .Q(x16));
  _64bitregister _64bitregister_17 (.D(WD), .CLK(CLK), .EN(EN16), .CLR(CLR), .Q(x17));
  _64bitregister _64bitregister_18 (.D(WD), .CLK(CLK), .EN(EN17), .CLR(CLR), .Q(x18));
  _64bitregister _64bitregister_19 (.D(WD), .CLK(CLK), .EN(EN18), .CLR(CLR), .Q(x19));
  _64bitregister _64bitregister_20 (.D(WD), .CLK(CLK), .EN(EN19), .CLR(CLR), .Q(x20));
  _64bitregister _64bitregister_21 (.D(WD), .CLK(CLK), .EN(EN20), .CLR(CLR), .Q(x21));
  _64bitregister _64bitregister_22 (.D(WD), .CLK(CLK), .EN(EN21), .CLR(CLR), .Q(x22));
  _64bitregister _64bitregister_23 (.D(WD), .CLK(CLK), .EN(EN22), .CLR(CLR), .Q(x23));
  _64bitregister _64bitregister_24 (.D(WD), .CLK(CLK), .EN(EN23), .CLR(CLR), .Q(x24));
  _64bitregister _64bitregister_25 (.D(WD), .CLK(CLK), .EN(EN24), .CLR(CLR), .Q(x25));
  _64bitregister _64bitregister_26 (.D(WD), .CLK(CLK), .EN(EN25), .CLR(CLR), .Q(x26));
  _64bitregister _64bitregister_27 (.D(WD), .CLK(CLK), .EN(EN26), .CLR(CLR), .Q(x27));
  _64bitregister _64bitregister_28 (.D(WD), .CLK(CLK), .EN(EN27), .CLR(CLR), .Q(x28));
  _64bitregister _64bitregister_29 (.D(WD), .CLK(CLK), .EN(EN28), .CLR(CLR), .Q(x29));
  _64bitregister _64bitregister_30 (.D(WD), .CLK(CLK), .EN(EN29), .CLR(CLR), .Q(x30));
  _64bitregister _64bitregister_31 (.D(WD), .CLK(CLK), .EN(EN30), .CLR(CLR), .Q(x31));

  assign x0 = {64{1'b0}};
endmodule
